# Fritzing sketch Sensor de Enchentes (saved by Fritzing 0.9.3b)
breadboards: 1

parts:
  R3 = Resistor [tolerance=±20% resistance=330 package="0402 [SMD]"]
  R1 = Resistor [tolerance=±5% resistance=471 package="0603 [SMD]"]
  Componente2 = Arduino Mega 2560 (Rev3)
  YF-S201_Flow_Meter1 = YF-S201 Water Flow Meter
  Water_Level_Sensor1 = Water Level Sensor
  A1 = NEO-6M GPS Module [part_number=GY-GPS6MV2]
  433T30D1 = 433T30D

nets:
  N1: R3.Pin_0, Componente2.D17_PWM/RX2
  N2: R3.Pin_1, R1.Pin_0, 433T30D1.RXD
  GND: R1.Pin_1, Componente2.GND, YF-S201_Flow_Meter1.GND, Water_Level_Sensor1.GND, A1.GND, 433T30D1.M0, 433T30D1.M1, 433T30D1.GND
  N3: Componente2.A0, Water_Level_Sensor1.SIG
  N4: Componente2.D19/RX1, A1.Rx
  N5: Componente2.D18/TX1, A1.Tx
  N6: Componente2.D16_PWM/TX2, 433T30D1.TXD
  VCC: Componente2.5V, YF-S201_Flow_Meter1.VCC, Water_Level_Sensor1.VCC, A1.Vcc, 433T30D1.VCC
  N7: Componente2.D2_PWM, YF-S201_Flow_Meter1.SIG

custom parts:
  YF-S201 Water Flow Meter: The YF-S201 Flow Meter. The input voltage is 5V to 24V (DC).
  Water Level Sensor: A water level sensor. This sensor operates at 3V to 5V. The Sig (signal) pin outputs an analogue signal that is in proportion to the amount of water in contact with the sensor.
  NEO-6M GPS Module: GY-GPS6MV2 NEO-6M GPS Module Module based on U-blox NEO-6M GPS engine, incorporating regulator for 3.3-5V DC input, MS621FE-compatible rechargeable battery for backup and EEPROM for storing configuration settings. Links: NEO-6 series product information page NEO-6 Datasheet
  433T30D: Long Distance Wireless Transceiver UART LoRa Module

// code stored in the sketch: Sensor de Enchentes.ino
// Definição de Rota é definida via terminal

#include <TinyGPS.h>

#define TIMEOUT 10000; // Valor para identificar Timeout por desconexão

// inicializando variáveis e objetos
TinyGPS gps1; // Objeto de classe de GPS
int levelSensorPin = A0; // Pino de sensor de nível de água
int flowSensorPin = 2; // Pino de sensor de fluxo de água
volatile long pulse;
unsigned long lastTime;
unsigned long lastFlowSignalTime; // Variável para armazenar tempo de último sinal do sensor de fluxo
unsigned long lastLevelSignalTime; // Variável para armazenar tempo de último sinal do sensor de nível
// Booleans para indicar desconexão
bool isDisconnectedFlow;
bool isDisconnectedLevel;

void setup(){
	pinMode(flowSensorPin, INPUT); // definindo modo do sensor de fluxo
	// inicializando portas seriais
	Serial.begin(9600);
	Serial1.begin(9600);
	Serial2.begin(9600);
	attachInterrupt(digitalPinToInterrupt(flowSensorPin), increasePulseCounter, RISING); // configuração de funcionamento e tratamento de dados do sensor de fluxo
	unsigned long lastFlowSignal = millis();
	unsigned long lastLevelSignal = millis();
}

void loop(){
	bool received = false; // booleano para informar estado de recebimento de dados do GPS
	while (Serial1.available()){
		char cIn = Serial1.read();
		received = gps1.encode(cIn); // check de recebimento de dados do GPS
	}
	if (received){
		// informações recebidas do GPS abaixo
		long latitude, longitude;
		unsigned long ageInfo; // Variável para tempo que os dados foram recebidos
		gps1.get_position(&latitude, &longitude, &ageInfo); // Receber localização em latitude e longitude
		
		// Dados referentes à data da informação abaixo
		int year;
		byte month, day, hour, minute, second, centisecond;
		gps1.crack_datertime(&year, &month, &day, &hour, &minute, &second, &centisecond); //  Receber Data e Horário
	}
	int flowSensorState = digitalRead(flowSensorPin);
	
	if(flowSensorState == HIGH){ // Checagem de conexão do sensor de fluxo
		lastFlowSignal = millis();
		isDisconnectedFlow = false;
	}

	if(millis() - lastFlowSignal > TIMEOUT && !isDisconnectedFlow){// Caso timeout tenha ocorrido
		isDisconnectedFlow = true;
		Serial2.println("Possível Disconexão! " + alerta(latitude, longitude, year, month, day, hour, minute, second, centisecond, ageInfo));
	}

	int levelSensorValue = analogRead(waterSensorPin); // Lendo valores do sensor de nível da água
	
	if(levelSensorValue >= 0 && levelSensorValue <= 1023){ // Checagem de conexão do sensor de nível
		lastLevelSignal = millis();
		isDisconnectedLevel = false;
	}

	if(millis() - lastLevelSignal > TIMEOUT && !isDisconnectedLevel){// Caso timeout tenha ocorrido
		isDisconnectedLevel = true;
		Serial2.println("Possível Disconexão! " + alerta(latitude, longitude, year, month, day, hour, minute, second, centisecond, ageInfo));
	}

	volume = 2.663 * pulse; // Volume passando pelo sensor de fluxo (mL)
	if (millis() - lastTime > 1000){ //Condição feita para identificar mL/s
		pulse = 0;
		lastTime = millis();
		if(levelSensorValue > 500 && volume > 1000){ // Condição para detectar se os níveis e fluxo da água estão fortes no nível de alerta
			Serial2.println("Alerta! " + alerta(latitude, longitude, year, month, day, hour, minute, second, centisecond, ageInfo));
			// Acima, envio de informações a respeito do alerta, incluindo localização e horário
		}
	}
}

void increasePulseCounter() {
	pulse++; // Função para incrementar contagem dos inputs do sensor de fluxo
}

// Função para retornar informações sobre alerta
String alerta(long latitude, long longitude, int year, byte month, byte day, byte hour, byte minute, byte second, byte centisecond, unsigned long ageInfo) {
	return "Latitude: " + latitude + "; Longitude: " + longitude + "\n" + day + "/" + month + "/" +  year + " " + hour + ":" + minute + ":" + second + "\nIdade da informação: " + ageInfo + "(ms)";
}
